// Logisim project diceRoll_display.circ as structural Verilog: 4 circuits, main circuit main
// 1
module main (
  input  [4:0] roll,
  input  reset,
  output [4:0] tens,
  output [4:0] ones
);

  wire clock_1_out, larger_10_comparator_1_selector, seven_seg_1_a, seven_seg_1_b, seven_seg_1_c,
       seven_seg_1_d, seven_seg_1_e, seven_seg_1_f, seven_seg_1_g, seven_seg_2_a, seven_seg_2_b,
       seven_seg_2_c, seven_seg_2_d, seven_seg_2_e, seven_seg_2_f, seven_seg_2_g;
  wire [4:0] adder_1_out, adder_2_out, multiplexer_1_out, multiplexer_2_out, subtract_circuit_1_result;

  Clock clock_1 (.out(clock_1_out));
  Multiplexer #(.width(5)) multiplexer_1 (
    .in0({5{1'b0}}), .in1(5'b00001), .out(multiplexer_1_out), .sel(larger_10_comparator_1_selector));
  Adder #(.width(5)) adder_1 (.a(multiplexer_1_out), .b(tens), .out(adder_1_out));  // open: cin, cout
  Adder #(.width(5)) adder_2 (.a(roll), .b(ones), .out(adder_2_out));  // open: cin, cout
  larger_10_comparator larger_10_comparator_1 (
    .v4(adder_2_out[4]), .v3(adder_2_out[3]), .v2(adder_2_out[2]), .v1(adder_2_out[1]), .v0(adder_2_out[0]),
    .selector(larger_10_comparator_1_selector));
  D_Flip_Flop d_ff_1 (.D(adder_1_out[0]), .clk(clock_1_out), .Q(tens[0]), .reset(reset));  // open: Qn, preset
  D_Flip_Flop d_ff_2 (.D(adder_1_out[1]), .clk(clock_1_out), .Q(tens[1]), .preset(reset), .reset(reset));  // open: Qn
  D_Flip_Flop d_ff_3 (.D(adder_1_out[2]), .clk(clock_1_out), .Q(tens[2]), .preset(reset), .reset(reset));  // open: Qn
  D_Flip_Flop d_ff_4 (.D(adder_1_out[3]), .clk(clock_1_out), .Q(tens[3]), .preset(reset), .reset(reset));  // open: Qn
  D_Flip_Flop d_ff_5 (.D(adder_1_out[4]), .clk(clock_1_out), .Q(tens[4]), .preset(reset), .reset(reset));  // open: Qn
  Multiplexer #(.width(5)) multiplexer_2 (
    .in0(adder_2_out), .in1(subtract_circuit_1_result), .out(multiplexer_2_out),
    .sel(larger_10_comparator_1_selector));
  D_Flip_Flop d_ff_6 (.D(multiplexer_2_out[0]), .clk(clock_1_out), .Q(ones[0]), .reset(reset));  // open: Qn, preset
  D_Flip_Flop d_ff_7 (
    .D(multiplexer_2_out[1]), .clk(clock_1_out), .Q(ones[1]), .preset(reset), .reset(reset));  // open: Qn
  D_Flip_Flop d_ff_8 (
    .D(multiplexer_2_out[2]), .clk(clock_1_out), .Q(ones[2]), .preset(reset), .reset(reset));  // open: Qn
  D_Flip_Flop d_ff_9 (
    .D(multiplexer_2_out[3]), .clk(clock_1_out), .Q(ones[3]), .preset(reset), .reset(reset));  // open: Qn
  D_Flip_Flop d_ff_10 (
    .D(multiplexer_2_out[4]), .clk(clock_1_out), .Q(ones[4]), .preset(reset), .reset(reset));  // open: Qn
  subtract_circuit subtract_circuit_1 (
    .sel(1'b1), .a0(adder_2_out[0]), .a1(adder_2_out[1]), .a2(adder_2_out[2]), .a3(adder_2_out[3]),
    .a4(adder_2_out[4]), .result(subtract_circuit_1_result));  // open: out_8
  _7_Segment_Display u_7_segment_display_1 (
    .g(seven_seg_2_g), .f(seven_seg_2_f), .a(seven_seg_2_a), .b(seven_seg_2_b), .e(seven_seg_2_e),
    .d(seven_seg_2_d), .c(seven_seg_2_c));  // open: dp
  _7_Segment_Display u_7_segment_display_2 (
    .g(seven_seg_1_g), .f(seven_seg_1_f), .a(seven_seg_1_a), .b(seven_seg_1_b), .e(seven_seg_1_e),
    .d(seven_seg_1_d), .c(seven_seg_1_c));  // open: dp
  seven_seg seven_seg_1 (
    .v3(ones[3]), .v2(ones[2]), .v1(ones[1]), .v0(ones[0]), .a(seven_seg_1_a), .b(seven_seg_1_b),
    .c(seven_seg_1_c), .d(seven_seg_1_d), .e(seven_seg_1_e), .f(seven_seg_1_f), .g(seven_seg_1_g));
  seven_seg seven_seg_2 (
    .v3(tens[3]), .v2(tens[2]), .v1(tens[1]), .v0(tens[0]), .a(seven_seg_2_a), .b(seven_seg_2_b),
    .c(seven_seg_2_c), .d(seven_seg_2_d), .e(seven_seg_2_e), .f(seven_seg_2_f), .g(seven_seg_2_g));
endmodule

module larger_10_comparator (
  input  v4,
  input  v3,
  input  v2,
  input  v1,
  input  v0,
  output selector
);

  wire and_1_out, and_2_out, not_1_out, not_2_out, not_3_out, not_4_out, not_5_out;

  not not_1 (not_1_out, v4);
  not not_2 (not_2_out, v3);
  not not_3 (not_3_out, v2);
  not not_4 (not_4_out, v1);
  not not_5 (not_5_out, v0);
  and and_1 (and_1_out, v3, v2);
  and and_2 (and_2_out, v3, v1);
  or or_1 (selector, v4, and_1_out, and_2_out);
endmodule

module subtract_circuit (
  input  sel,
  input  a0,
  input  a1,
  input  a2,
  input  a3,
  input  a4,
  output [4:0] result,
  output out_8
);

  wire adder_1_cout, adder_2_cout, adder_3_cout, adder_4_cout, xor_1_out, xor_2_out, xor_3_out, xor_4_out,
       xor_5_out;

  xor xor_1 (xor_1_out, 1'b0, sel);
  xor xor_2 (xor_2_out, 1'b1, sel);
  xor xor_3 (xor_3_out, 1'b0, sel);
  xor xor_4 (xor_4_out, 1'b1, sel);
  xor xor_5 (xor_5_out, 1'b0, sel);
  Adder #(.width(1)) adder_1 (.a(a0), .b(xor_1_out), .out(result[0]), .cin(sel), .cout(adder_1_cout));
  Adder #(.width(1)) adder_2 (.a(a1), .b(xor_2_out), .out(result[1]), .cin(adder_1_cout), .cout(adder_2_cout));
  Adder #(.width(1)) adder_3 (.a(a2), .b(xor_3_out), .out(result[2]), .cin(adder_2_cout), .cout(adder_3_cout));
  Adder #(.width(1)) adder_4 (.a(a3), .b(xor_4_out), .out(result[3]), .cin(adder_3_cout), .cout(adder_4_cout));
  Adder #(.width(1)) adder_5 (.a(a4), .b(xor_5_out), .out(result[4]), .cin(adder_4_cout), .cout(out_8));
endmodule

module seven_seg (
  input  v3,
  input  v2,
  input  v1,
  input  v0,
  output a,
  output b,
  output c,
  output d,
  output e,
  output f,
  output g
);

  wire nand_1_out, nand_2_out, nand_3_out, nand_4_out, nand_5_out, nand_6_out, nand_7_out, nand_8_out,
       nand_9_out, nand_10_out, nand_11_out, nand_12_out, nand_13_out, nand_14_out, nand_15_out, nand_16_out,
       nand_17_out, nand_18_out, nand_19_out, nand_20_out, nand_21_out, nand_22_out, nand_23_out,
       nand_24_out, nand_25_out, nand_26_out, nand_27_out, nand_28_out, nand_29_out, nand_30_out,
       nand_31_out, nand_32_out, nand_33_out, nand_34_out, nand_35_out, nand_36_out, nand_37_out,
       nand_38_out, nand_39_out, nand_40_out, nand_41_out, nand_42_out, nand_43_out, nand_44_out,
       nand_45_out, nand_46_out, nand_47_out, nand_48_out, nand_49_out, nand_50_out, nand_51_out,
       nand_52_out, nand_53_out, nand_54_out, nand_55_out, nand_56_out, nand_57_out, nand_58_out,
       nand_59_out, nand_60_out, nand_61_out, nand_62_out, nand_63_out, nand_64_out, nand_65_out,
       nand_66_out, nand_67_out, nand_68_out, nand_69_out, nand_70_out, nand_71_out, nand_72_out,
       nand_73_out, nand_74_out, nand_75_out, nand_76_out, nand_77_out, nand_78_out, nand_79_out,
       nand_80_out, nand_81_out, nand_82_out, nand_83_out, nand_84_out, nand_85_out, nand_86_out,
       nand_87_out, nand_88_out, nand_89_out, nand_90_out, nand_91_out, nand_92_out, nand_93_out,
       nand_94_out, nand_95_out, nand_96_out, nand_97_out, nand_98_out, nand_99_out, nand_100_out,
       nand_101_out, nand_102_out, nand_103_out, nand_104_out, nand_106_out, nand_107_out, nand_108_out,
       nand_109_out, nand_110_out, nand_111_out, nand_112_out, nand_113_out, nand_114_out, nand_115_out,
       nand_116_out, nand_117_out, nand_118_out, nand_119_out, nand_120_out, nand_121_out, nand_122_out,
       nand_123_out, nand_124_out, nand_125_out, nand_126_out, nand_127_out, nand_128_out, nand_129_out,
       nand_130_out, nand_131_out, nand_132_out, nand_133_out, nand_134_out, nand_136_out, nand_137_out,
       nand_138_out, nand_139_out, nand_141_out, nand_142_out, nand_143_out, nand_144_out, nand_145_out,
       nand_146_out, nand_147_out, nand_148_out;

  nand nand_1 (nand_1_out, v2, v2);
  nand nand_2 (nand_2_out, v3, v3);
  nand nand_3 (nand_3_out, v1, v1);
  nand nand_4 (nand_4_out, v3, v3);
  nand nand_5 (nand_5_out, v1, v1);
  nand nand_6 (nand_6_out, v3, v3);
  nand nand_7 (nand_7_out, v3, v3);
  nand nand_8 (nand_8_out, v2, v2);
  nand nand_9 (nand_9_out, v2, v2);
  nand nand_10 (nand_10_out, v2, v2);
  nand nand_11 (nand_11_out, v0, v0);
  nand nand_12 (nand_12_out, v0, v0);
  nand nand_13 (nand_13_out, v3, v3);
  nand nand_14 (nand_14_out, v2, v2);
  nand nand_15 (nand_15_out, v0, v0);
  nand nand_16 (nand_16_out, v3, v3);
  nand nand_17 (nand_17_out, v3, nand_1_out);
  nand nand_18 (nand_18_out, nand_2_out, nand_3_out);
  nand nand_19 (nand_19_out, nand_4_out, nand_5_out);
  nand nand_20 (nand_20_out, nand_6_out, v0);
  nand nand_21 (nand_21_out, nand_7_out, nand_8_out);
  nand nand_22 (nand_22_out, nand_9_out, v1);
  nand nand_23 (nand_23_out, nand_10_out, nand_11_out);
  nand nand_24 (nand_24_out, v1, nand_12_out);
  nand nand_25 (nand_25_out, v3, v1);
  nand nand_26 (nand_26_out, v3, v2);
  nand nand_27 (nand_27_out, nand_13_out, v2);
  nand nand_28 (nand_28_out, nand_14_out, v1);
  nand nand_29 (nand_29_out, v1, nand_15_out);
  nand nand_30 (nand_30_out, nand_16_out, v2);
  nand nand_31 (nand_31_out, v2, v2);
  nand nand_32 (nand_32_out, v0, v0);
  nand nand_33 (nand_33_out, v3, v3);
  nand nand_34 (nand_34_out, v3, v3);
  nand nand_35 (nand_35_out, nand_17_out, nand_17_out);
  nand nand_36 (nand_36_out, v1, v1);
  nand nand_37 (nand_37_out, v3, v3);
  nand nand_38 (nand_38_out, v2, v2);
  nand nand_39 (nand_39_out, nand_18_out, nand_18_out);
  nand nand_40 (nand_40_out, v0, v0);
  nand nand_41 (nand_41_out, v3, v3);
  nand nand_42 (nand_42_out, v1, v1);
  nand nand_43 (nand_43_out, nand_19_out, nand_20_out);
  nand nand_44 (nand_44_out, v1, v1);
  nand nand_45 (nand_45_out, v3, v3);
  nand nand_46 (nand_46_out, v2, v2);
  nand nand_47 (nand_47_out, nand_21_out, nand_21_out);
  nand nand_48 (nand_48_out, v0, v0);
  nand nand_49 (nand_49_out, nand_22_out, nand_22_out);
  nand nand_50 (nand_50_out, v1, v1);
  nand nand_51 (nand_51_out, v1, v1);
  nand nand_52 (nand_52_out, nand_23_out, nand_24_out);
  nand nand_53 (nand_53_out, nand_25_out, nand_26_out);
  nand nand_54 (nand_54_out, v1, v1);
  nand nand_55 (nand_55_out, v0, v0);
  nand nand_56 (nand_56_out, nand_27_out, nand_27_out);
  nand nand_57 (nand_57_out, v1, v1);
  nand nand_58 (nand_58_out, nand_28_out, nand_29_out);
  nand nand_59 (nand_59_out, nand_30_out, nand_30_out);
  nand nand_60 (nand_60_out, v1, v1);
  nand nand_61 (nand_61_out, v2, v2);
  nand nand_62 (nand_62_out, nand_31_out, nand_32_out);
  nand nand_63 (nand_63_out, nand_33_out, v1);
  nand nand_64 (nand_64_out, nand_34_out, v2);
  nand nand_65 (nand_65_out, v2, v1);
  nand nand_66 (nand_66_out, nand_35_out, nand_36_out);
  nand nand_67 (nand_67_out, nand_37_out, nand_38_out);
  nand nand_68 (nand_68_out, nand_39_out, nand_40_out);
  nand nand_69 (nand_69_out, nand_41_out, v1);
  nand nand_70 (nand_70_out, v3, nand_42_out);
  nand nand_71 (nand_71_out, nand_43_out, nand_43_out);
  nand nand_72 (nand_72_out, nand_44_out, v0);
  nand nand_73 (nand_73_out, nand_45_out, v2);
  nand nand_74 (nand_74_out, v3, nand_46_out);
  nand nand_75 (nand_75_out, nand_47_out, nand_48_out);
  nand nand_76 (nand_76_out, nand_49_out, v0);
  nand nand_77 (nand_77_out, v2, nand_50_out);
  nand nand_78 (nand_78_out, v2, v1);
  nand nand_79 (nand_79_out, v3, nand_51_out);
  nand nand_80 (nand_80_out, nand_52_out, nand_52_out);
  nand nand_81 (nand_81_out, nand_53_out, nand_53_out);
  nand nand_82 (nand_82_out, nand_54_out, nand_55_out);
  nand nand_83 (nand_83_out, nand_56_out, nand_57_out);
  nand nand_84 (nand_84_out, nand_58_out, nand_58_out);
  nand nand_85 (nand_85_out, nand_59_out, nand_60_out);
  nand nand_86 (nand_86_out, v3, nand_61_out);
  nand nand_87 (nand_87_out, v3, v0);
  nand nand_88 (nand_88_out, nand_62_out, nand_63_out);
  nand nand_89 (nand_89_out, nand_64_out, nand_64_out);
  nand nand_90 (nand_90_out, nand_65_out, nand_66_out);
  nand nand_91 (nand_91_out, v0, v0);
  nand nand_92 (nand_92_out, nand_67_out, nand_68_out);
  nand nand_93 (nand_93_out, v2, v2);
  nand nand_94 (nand_94_out, v0, v0);
  nand nand_95 (nand_95_out, nand_69_out, nand_69_out);
  nand nand_96 (nand_96_out, nand_70_out, nand_70_out);
  nand nand_97 (nand_97_out, nand_71_out, nand_72_out);
  nand nand_98 (nand_98_out, nand_73_out, nand_74_out);
  nand nand_99 (nand_99_out, nand_75_out, nand_76_out);
  nand nand_100 (nand_100_out, nand_77_out, nand_77_out);
  nand nand_101 (nand_101_out, nand_78_out, nand_78_out);
  nand nand_102 (nand_102_out, v0, v0);
  nand nand_103 (nand_103_out, nand_79_out, nand_79_out);
  nand nand_104 (nand_104_out, v0, v0);
  nand nand_105 (e, nand_80_out, nand_81_out);
  nand nand_106 (nand_106_out, nand_82_out, nand_83_out);
  nand nand_107 (nand_107_out, v0, v0);
  nand nand_108 (nand_108_out, v2, v2);
  nand nand_109 (nand_109_out, nand_84_out, nand_85_out);
  nand nand_110 (nand_110_out, nand_86_out, nand_87_out);
  nand nand_111 (nand_111_out, nand_88_out, nand_88_out);
  nand nand_112 (nand_112_out, nand_89_out, v0);
  nand nand_113 (nand_113_out, nand_90_out, nand_90_out);
  nand nand_114 (nand_114_out, v3, nand_91_out);
  nand nand_115 (nand_115_out, nand_92_out, nand_92_out);
  nand nand_116 (nand_116_out, nand_93_out, nand_94_out);
  nand nand_117 (nand_117_out, nand_95_out, v0);
  nand nand_118 (nand_118_out, nand_96_out, v0);
  nand nand_119 (nand_119_out, nand_97_out, nand_97_out);
  nand nand_120 (nand_120_out, nand_98_out, nand_98_out);
  nand nand_121 (nand_121_out, nand_99_out, nand_99_out);
  nand nand_122 (nand_122_out, nand_100_out, v0);
  nand nand_123 (nand_123_out, nand_101_out, nand_102_out);
  nand nand_124 (nand_124_out, nand_103_out, nand_104_out);
  nand nand_125 (nand_125_out, nand_106_out, nand_106_out);
  nand nand_126 (nand_126_out, v2, nand_107_out);
  nand nand_127 (nand_127_out, v3, nand_108_out);
  nand nand_128 (nand_128_out, v3, v1);
  nand nand_129 (nand_129_out, nand_109_out, nand_109_out);
  nand nand_130 (nand_130_out, nand_110_out, nand_110_out);
  nand nand_131 (nand_131_out, nand_111_out, nand_112_out);
  nand nand_132 (nand_132_out, nand_113_out, nand_114_out);
  nand nand_133 (nand_133_out, nand_115_out, nand_116_out);
  nand nand_134 (nand_134_out, nand_117_out, nand_118_out);
  nand nand_135 (c, nand_119_out, nand_120_out);
  nand nand_136 (nand_136_out, nand_121_out, nand_122_out);
  nand nand_137 (nand_137_out, nand_123_out, nand_124_out);
  nand nand_138 (nand_138_out, nand_125_out, nand_126_out);
  nand nand_139 (nand_139_out, nand_127_out, nand_128_out);
  nand nand_140 (g, nand_129_out, nand_130_out);
  nand nand_141 (nand_141_out, nand_131_out, nand_131_out);
  nand nand_142 (nand_142_out, nand_132_out, nand_132_out);
  nand nand_143 (nand_143_out, nand_133_out, nand_133_out);
  nand nand_144 (nand_144_out, nand_134_out, nand_134_out);
  nand nand_145 (nand_145_out, nand_136_out, nand_136_out);
  nand nand_146 (nand_146_out, nand_137_out, nand_137_out);
  nand nand_147 (nand_147_out, nand_138_out, nand_138_out);
  nand nand_148 (nand_148_out, nand_139_out, nand_139_out);
  nand nand_149 (a, nand_141_out, nand_142_out);
  nand nand_150 (b, nand_143_out, nand_144_out);
  nand nand_151 (d, nand_145_out, nand_146_out);
  nand nand_152 (f, nand_147_out, nand_148_out);
endmodule
